// Logisim project WITCPU.circ as structural Verilog: 9 circuits, main circuit RegisterR0-3
module main (
);

  wire and_1_out, and_2_out, bus_controller_1_alu_enable, bus_controller_1_ram_read,
       bus_controller_1_ram_write, bus_controller_1_register_write, clock_1_out, not_1_out, t_ff_1_q;
  wire [3:0] decoder_1_opcode, decoder_1_rd, decoder_1_rx, decoder_1_ry;
  wire [7:0] bus_controller_1_address, decoder_1_mm, multiplexer_1_out, pc_controller_1_next, PC_q;
  wire [15:0] instructions_q, ram_1_data, register_1_value___rx, register_1_value___ry;

  Clock_part clock_1 (.out(clock_1_out));
  not not_1 (not_1_out, clock_1_out);
  T_Flip_Flop t_ff_1 (.clk(not_1_out), .T(1'b1), .Q(t_ff_1_q));  // open: Qn, preset, reset, en
  Multiplexer #(.width(8), .enable("false")) multiplexer_1 (
    .in0(PC_q), .in1(bus_controller_1_address), .out(multiplexer_1_out), .sel(t_ff_1_q));
  and and_1 (and_1_out, ~t_ff_1_q, clock_1_out);  // AND_Gate
  and and_2 (and_2_out, ~clock_1_out, t_ff_1_q);  // AND_Gate
  RAM #(.dataWidth(16), .bus("separate")) ram_1 (
    .addr(multiplexer_1_out), .data(ram_1_data), .str(bus_controller_1_ram_write), .clk(clock_1_out),
    .ld(bus_controller_1_ram_read));  // open: din, sel, clr
  Register_part #(.width(16)) instructions (.D(ram_1_data), .Q(instructions_q), .clk(and_1_out));  // open: en, clr
  Register_part PC (.D(pc_controller_1_next), .Q(PC_q), .clk(and_2_out));  // open: en, clr
  Decoder decoder_1 (
    .Instruction(instructions_q), .opcode(decoder_1_opcode), .Rd(decoder_1_rd), .Rx(decoder_1_rx),
    .Ry(decoder_1_ry), .mm(decoder_1_mm));
  Bus_Controller bus_controller_1 (
    .imm(decoder_1_mm), .data(register_1_value___rx), .opcode(decoder_1_opcode), .Cycle(t_ff_1_q),
    .Clock(clock_1_out), .address(bus_controller_1_address), .ALU_enable(bus_controller_1_alu_enable),
    .Register_write(bus_controller_1_register_write), .Ram_read(bus_controller_1_ram_read),
    .Ram_write(bus_controller_1_ram_write));
  Register register_1 (
    .Data(ram_1_data), .tick(bus_controller_1_register_write), .Rd(decoder_1_rd), .Rx(decoder_1_rx),
    .Ry(decoder_1_ry), .Value___Rx(register_1_value___rx), .Value___Ry(register_1_value___ry));
  ALU alu_1 (
    .Enable(bus_controller_1_alu_enable), .opcode(decoder_1_opcode), .x(register_1_value___rx),
    .y(register_1_value___ry), .imm(decoder_1_mm), .out_6(ram_1_data));
  PC_Controller pc_controller_1 (
    .Rx(register_1_value___rx), .opcode(decoder_1_opcode), .imm(decoder_1_mm), .prev(PC_q),
    .Next(pc_controller_1_next));
endmodule

module RegisterR0_3 (
  input  [15:0] Data,
  input  tick,
  input  [1:0] Rx,
  input  [1:0] Ry,
  input  [1:0] Rd,
  output [15:0] V,
  output [15:0] out_7
);

  wire demultiplexer_1_out0, demultiplexer_1_out1, demultiplexer_1_out2, demultiplexer_1_out3;
  wire [15:0] register_1_q, register_2_q, register_3_q, register_4_q;

  Demultiplexer #(.select(2)) demultiplexer_1 (
    .out0(demultiplexer_1_out0), .out1(demultiplexer_1_out1), .out2(demultiplexer_1_out2),
    .out3(demultiplexer_1_out3), .in(tick), .sel(Rd));  // open: en
  Register_part #(.width(16)) register_1 (
    .D({16{1'b0}}), .Q(register_1_q), .clk(demultiplexer_1_out0));  // open: en, clr
  Register_part #(.width(16)) register_2 (.D(Data), .Q(register_2_q), .clk(demultiplexer_1_out1));  // open: en, clr
  Register_part #(.width(16)) register_3 (.D(Data), .Q(register_3_q), .clk(demultiplexer_1_out2));  // open: en, clr
  Register_part #(.width(16)) register_4 (.D(Data), .Q(register_4_q), .clk(demultiplexer_1_out3));  // open: en, clr
  Multiplexer #(.select(2), .width(16)) multiplexer_1 (
    .in0(register_1_q), .in1(register_2_q), .in2(register_3_q), .in3(register_4_q), .out(V), .sel(Rx));  // open: en
  Multiplexer #(.select(2), .width(16)) multiplexer_2 (
    .in0(register_1_q), .in1(register_2_q), .in2(register_3_q), .in3(register_4_q), .out(out_7), .sel(Ry));  // open: en
endmodule

module group (
  input  [15:0] Data,
  input  tick,
  input  [1:0] Rx,
  input  [1:0] Ry,
  input  [1:0] Rd,
  output [15:0] Rx_2,
  output [15:0] Ry_2
);

  wire demultiplexer_1_out0, demultiplexer_1_out1, demultiplexer_1_out2, demultiplexer_1_out3;
  wire [15:0] register_1_q, register_2_q, register_3_q, register_4_q;

  Demultiplexer #(.select(2)) demultiplexer_1 (
    .out0(demultiplexer_1_out0), .out1(demultiplexer_1_out1), .out2(demultiplexer_1_out2),
    .out3(demultiplexer_1_out3), .in(tick), .sel(Rd));  // open: en
  Register_part #(.width(16)) register_1 (.D(Data), .Q(register_1_q), .clk(demultiplexer_1_out0));  // open: en, clr
  Register_part #(.width(16)) register_2 (.D(Data), .Q(register_2_q), .clk(demultiplexer_1_out1));  // open: en, clr
  Register_part #(.width(16)) register_3 (.D(Data), .Q(register_3_q), .clk(demultiplexer_1_out2));  // open: en, clr
  Register_part #(.width(16)) register_4 (.D(Data), .Q(register_4_q), .clk(demultiplexer_1_out3));  // open: en, clr
  Multiplexer #(.select(2), .width(16)) multiplexer_1 (
    .in0(register_1_q), .in1(register_2_q), .in2(register_3_q), .in3(register_4_q), .out(Rx_2), .sel(Rx));  // open: en
  Multiplexer #(.select(2), .width(16)) multiplexer_2 (
    .in0(register_1_q), .in1(register_2_q), .in2(register_3_q), .in3(register_4_q), .out(Ry_2), .sel(Ry));  // open: en
endmodule

module ALU (
  input  Enable,
  input  [3:0] opcode,
  input  [15:0] x,
  input  [15:0] y,
  input  [7:0] imm,
  output [15:0] out_6
);

  wire [15:0] adder_1_out, and_1_out, divider_1_out, multiplier_1_out, or_1_out, subtractor_1_out, xnor_1_out;

  Adder #(.width(16)) adder_1 (.a(x), .b(y), .out(adder_1_out));  // open: cin, cout
  Subtractor #(.width(16)) subtractor_1 (.a(x), .b(y), .out(subtractor_1_out));  // open: bin, bout
  Multiplier #(.width(16)) multiplier_1 (.a(x), .b(y), .out(multiplier_1_out));  // open: cin, cout
  Divider #(.width(16)) divider_1 (.a(x), .b(y), .out(divider_1_out));  // open: upper, rem
  assign and_1_out = x & y;  // AND_Gate and_1, 16 bits wide
  assign or_1_out = x | y;  // OR_Gate or_1, 16 bits wide
  assign xnor_1_out = ~(x ^ y);  // XNOR_Gate xnor_1, 16 bits wide
  Multiplexer #(.select(3), .width(16)) multiplexer_1 (
    .in0(adder_1_out), .in1(subtractor_1_out), .in2(multiplier_1_out), .in3(divider_1_out), .in4(and_1_out),
    .in5(or_1_out), .in6(xnor_1_out), .in7({{9{imm[7]}}, imm[6:0]}), .out(out_6), .sel(opcode[2:0]),
    .en(Enable));
endmodule

// Decode
module Decoder (
  input  [15:0] Instruction,
  output [3:0] opcode,
  output [3:0] Rd,
  output [3:0] Rx,
  output [3:0] Ry,
  output [7:0] mm
);

  Multiplexer #(.width(4)) multiplexer_1 (
    .in0(Instruction[3:0]), .in1(Instruction[7:4]), .out(Ry), .sel(Instruction[15]));  // open: en

  assign mm = Instruction[7:0];
  assign opcode = Instruction[15:12];
  assign Rd = Instruction[11:8];
  assign Rx = Instruction[7:4];

  // Notes on the sheet:
  //   Instruction: pull=up
endmodule

// PC
module PC_Controller (
  input  [15:0] Rx,
  input  [3:0] opcode,
  input  [7:0] imm,
  input  [7:0] prev,
  output [7:0] Next
);

  wire and_1_out, comparator_1_eq, comparator_1_gt, comparator_1_lt, multiplexer_1_out, not_1_out, not_2_out;
  wire [7:0] adder_1_out;

  Comparator #(.width(16)) comparator_1 (
    .a(Rx), .b({16{1'b0}}), .gt(comparator_1_gt), .eq(comparator_1_eq), .lt(comparator_1_lt));
  Adder adder_1 (.a(prev), .b(8'h1), .out(adder_1_out));  // open: cin, cout
  not not_1 (not_1_out, comparator_1_eq);
  Multiplexer #(.select(2)) multiplexer_1 (
    .in0(comparator_1_eq), .in1(not_1_out), .in2(comparator_1_gt), .in3(comparator_1_lt),
    .out(multiplexer_1_out), .sel(opcode[1:0]));  // open: en
  not not_2 (not_2_out, opcode[2]);
  and and_1 (and_1_out, multiplexer_1_out, not_2_out, opcode[3]);
  Multiplexer #(.width(8)) multiplexer_2 (.in0(adder_1_out), .in1(imm), .out(Next), .sel(and_1_out));  // open: en
endmodule

// Clk
module Clock (
  output out_1
);

  wire not_1_out;

  not not_1 (not_1_out, out_1);
  Clock_part clock_1 (.out(out_1));
  T_Flip_Flop t_ff_1 (.clk(not_1_out), .T(1'b1));  // open: Q, Qn, preset, reset, en
endmodule

module Register (
  input  [15:0] Data,
  input  tick,
  input  [3:0] Rd,
  input  [3:0] Rx,
  input  [3:0] Ry,
  output [15:0] Value___Rx,
  output [15:0] Value___Ry
);

  wire demultiplexer_1_out0, demultiplexer_1_out1, demultiplexer_1_out2, demultiplexer_1_out3;
  wire [1:0] demultiplexer_2_out0, demultiplexer_2_out1, demultiplexer_2_out2, demultiplexer_2_out3;
  wire [15:0] R0_3_out_7, R0_3_v, R4_7_rx_2, R4_7_ry_2, R8_b_rx_2, R8_b_ry_2, Rc_f_rx_2, Rc_f_ry_2;

  Demultiplexer #(.select(2)) demultiplexer_1 (
    .out0(demultiplexer_1_out0), .out1(demultiplexer_1_out1), .out2(demultiplexer_1_out2),
    .out3(demultiplexer_1_out3), .in(tick), .sel(Rd[3:2]));  // open: en
  Demultiplexer #(.select(2), .width(2)) demultiplexer_2 (
    .out0(demultiplexer_2_out0), .out1(demultiplexer_2_out1), .out2(demultiplexer_2_out2),
    .out3(demultiplexer_2_out3), .in(Rd[1:0]), .sel(Rd[3:2]));  // open: en
  RegisterR0_3 R0_3 (
    .Data(Data), .tick(demultiplexer_1_out0), .Rx(Rx[1:0]), .Ry(Ry[1:0]), .Rd(demultiplexer_2_out0),
    .V(R0_3_v), .out_7(R0_3_out_7));
  group R4_7 (
    .Data(Data), .tick(demultiplexer_1_out1), .Rx(Rx[1:0]), .Ry(Ry[1:0]), .Rd(demultiplexer_2_out1),
    .Rx_2(R4_7_rx_2), .Ry_2(R4_7_ry_2));
  group R8_b (
    .Data(Data), .tick(demultiplexer_1_out2), .Rx(Rx[1:0]), .Ry(Ry[1:0]), .Rd(demultiplexer_2_out2),
    .Rx_2(R8_b_rx_2), .Ry_2(R8_b_ry_2));
  group Rc_f (
    .Data(Data), .tick(demultiplexer_1_out3), .Rx(Rx[1:0]), .Ry(Ry[1:0]), .Rd(demultiplexer_2_out3),
    .Rx_2(Rc_f_rx_2), .Ry_2(Rc_f_ry_2));
  Multiplexer #(.select(2), .width(16)) multiplexer_1 (
    .in0(R0_3_v), .in1(R4_7_rx_2), .in2(R8_b_rx_2), .in3(Rc_f_rx_2), .out(Value___Rx), .sel(Rx[3:2]));  // open: en
  Multiplexer #(.select(2), .width(16)) multiplexer_2 (
    .in0(R0_3_out_7), .in1(R4_7_ry_2), .in2(R8_b_ry_2), .in3(Rc_f_ry_2), .out(Value___Ry), .sel(Ry[3:2]));  // open: en
endmodule

// Bus
module Bus_Controller (
  input  [7:0] imm,
  input  [15:0] data,
  input  [3:0] opcode,
  input  Cycle,
  input  Clock,
  output [7:0] address,
  output ALU_enable,
  output Register_write,
  output Ram_read,
  output Ram_write
);

  wire and_1_out, and_3_out, and_5_out, and_6_out;

  and and_1 (and_1_out, Clock, Cycle);
  Multiplexer #(.width(8)) multiplexer_1 (.in0(imm), .in1(data[7:0]), .out(address), .sel(opcode[0]));  // open: en
  and and_2 (ALU_enable, ~opcode[3], Cycle);  // AND_Gate
  and and_3 (and_3_out, ~opcode[1], opcode[2], opcode[3]);  // AND_Gate
  and and_4 (Ram_write, and_1_out, opcode[1], opcode[2], opcode[3]);
  and and_5 (and_5_out, ALU_enable, Clock);
  and and_6 (and_6_out, and_3_out, and_1_out);
  or or_1 (Ram_read, and_6_out, ~Cycle);  // OR_Gate
  or or_2 (Register_write, and_5_out, and_3_out);
endmodule
