// Logisim project lab3.circ as structural Verilog: 1 circuit, main circuit main
module main (
  input  [2:0] X_Y_Z,
  input  [2:0] C_A_B
);

  wire multiplexer_1_out, multiplexer_2_out, multiplexer_3_out;

  Multiplexer #(.select(3)) multiplexer_1 (
    .in0(1'b0), .in1(1'b0), .in2(1'b0), .in3(1'b1), .in4(1'b0), .in5(1'b1), .in6(1'b1), .in7(1'b1),
    .out(multiplexer_1_out), .sel(X_Y_Z));  // open: en
  LED Majority_Out (.in(multiplexer_1_out));
  Multiplexer #(.select(3)) multiplexer_2 (
    .in0(1'b0), .in1(1'b1), .in2(1'b1), .in3(1'b0), .in4(1'b1), .in5(1'b0), .in6(1'b0), .in7(1'b1),
    .out(multiplexer_2_out), .sel(C_A_B));  // open: en
  Multiplexer #(.select(3)) multiplexer_3 (
    .in0(1'b0), .in1(1'b0), .in2(1'b0), .in3(1'b1), .in4(1'b0), .in5(1'b1), .in6(1'b1), .in7(1'b1),
    .out(multiplexer_3_out), .sel(C_A_B));  // open: en
  LED sum (.in(multiplexer_2_out));
  LED Cout (.in(multiplexer_3_out));
endmodule
