// Logisim project lab4.circ as structural Verilog: 5 circuits, main circuit D1
module main (
  input  in1,
  input  in2,
  output F,
  output W,
  output G,
  output C
);

  wire and_1_out, clock_1_out, D1_out_7, D2_out_7, D3_x, T_x;

  T T (.A0(F), .A1(W), .A2(G), .A3(C), .A4(in1), .A5(in2), .x(T_x));
  D1 D1 (.A0(F), .A1(W), .A2(G), .A3(C), .A4(in1), .A5(in2), .out_7(D1_out_7));
  D2 D2 (.A0(F), .A1(W), .A2(G), .A3(C), .A4(in1), .A5(in2), .out_7(D2_out_7));
  D3 D3 (.A0(F), .A1(W), .A2(G), .A3(C), .A4(in1), .A5(in2), .x(D3_x));
  Clock clock_1 (.out(clock_1_out));
  T_Flip_Flop T_2 (.clk(clock_1_out), .T(T_x), .Q(F));  // open: Qn, preset, reset, en
  D_Flip_Flop D1_2 (.clk(clock_1_out), .D(D1_out_7), .Q(W));  // open: Qn, preset, en, reset
  D_Flip_Flop D2_2 (.clk(clock_1_out), .D(D2_out_7), .Q(G));  // open: Qn, preset, en, reset
  D_Flip_Flop D3_2 (.clk(clock_1_out), .D(D3_x), .Q(C));  // open: Qn, preset, en, reset
  LED GOAL (.in(and_1_out));
  and and_1 (and_1_out, F, W, G, C);
endmodule

module D1 (
  input  A0,
  input  A1,
  input  A2,
  input  A3,
  input  A4,
  input  A5,
  output out_7
);

  wire and_1_out, and_2_out, and_3_out, and_4_out, and_5_out, and_6_out, and_7_out, and_8_out, and_9_out;

  and and_1 (and_1_out, ~A0, ~A1, A2, ~A3, ~A4, A5);  // AND_Gate
  and and_2 (and_2_out, A0, A1, A2, ~A3, A4, ~A5);  // AND_Gate
  and and_3 (and_3_out, ~A0, A1, ~A2, ~A3, A4, ~A5);  // AND_Gate
  and and_4 (and_4_out, ~A0, A1, ~A2, ~A3, A4, A5);  // AND_Gate
  and and_5 (and_5_out, A0, A1, ~A2, A3, A4, A5);  // AND_Gate
  and and_6 (and_6_out, ~A0, A1, ~A2, A3, ~A4, ~A5);  // AND_Gate
  and and_7 (and_7_out, ~A0, A1, ~A2, A3, A4, ~A5);  // AND_Gate
  and and_8 (and_8_out, ~A0, ~A1, ~A2, A3, ~A4, A5);  // AND_Gate
  and and_9 (and_9_out, A0, A1, ~A2, A3, ~A4, ~A5);  // AND_Gate
  or or_1 (out_7, and_1_out, and_2_out, and_3_out, and_4_out, and_9_out, and_5_out, and_6_out, and_7_out, and_8_out);
endmodule

module D2 (
  input  A0,
  input  A1,
  input  A2,
  input  A3,
  input  A4,
  input  A5,
  output out_7
);

  wire and_1_out, and_2_out, and_3_out, and_4_out, and_5_out, and_6_out, and_7_out, and_8_out, and_9_out,
       and_10_out;

  and and_1 (and_1_out, A0, ~A1, A2, A3, A4, A5);  // AND_Gate
  and and_2 (and_2_out, ~A0, ~A1, ~A2, A3, A4, ~A5);  // AND_Gate
  and and_3 (and_3_out, ~A0, ~A1, ~A2, ~A3, A4, ~A5);  // AND_Gate
  and and_4 (and_4_out, A0, ~A1, A2, ~A3, ~A4, ~A5);  // AND_Gate
  and and_5 (and_5_out, ~A0, ~A1, A2, ~A3, ~A4, ~A5);  // AND_Gate
  and and_6 (and_6_out, ~A0, ~A1, A2, ~A3, ~A4, A5);  // AND_Gate
  and and_7 (and_7_out, A0, A1, A2, ~A3, ~A4, A5);  // AND_Gate
  and and_8 (and_8_out, ~A0, A1, ~A2, ~A3, A4, ~A5);  // AND_Gate
  and and_9 (and_9_out, ~A0, ~A1, A2, ~A3, A4, A5);  // AND_Gate
  and and_10 (and_10_out, ~A0, A1, ~A2, A3, A4, ~A5);  // AND_Gate
  or or_1 (out_7, and_3_out, and_4_out, and_5_out, and_6_out, and_9_out, and_7_out, and_8_out, and_10_out, and_1_out, and_2_out);
endmodule

module D3 (
  input  A0,
  input  A1,
  input  A2,
  input  A3,
  input  A4,
  input  A5,
  output x
);

  wire and_1_out, and_2_out, and_3_out, and_4_out, and_5_out, and_6_out, and_7_out, and_8_out, and_9_out,
       not_1_out, not_2_out, not_3_out, not_4_out, not_5_out, not_6_out, not_7_out, not_8_out, not_9_out,
       not_10_out, not_11_out, not_12_out, not_13_out, not_14_out, not_15_out, not_16_out, not_17_out,
       not_18_out, not_19_out, not_20_out, not_21_out, not_22_out, not_23_out, not_24_out, not_25_out,
       not_26_out, not_27_out, not_28_out;

  not not_1 (not_1_out, A0);
  not not_2 (not_2_out, A1);
  not not_3 (not_3_out, A3);
  not not_4 (not_4_out, A0);
  not not_5 (not_5_out, A2);
  not not_6 (not_6_out, A3);
  not not_7 (not_7_out, A2);
  not not_8 (not_8_out, A4);
  not not_9 (not_9_out, A5);
  not not_10 (not_10_out, A2);
  not not_11 (not_11_out, A4);
  not not_12 (not_12_out, A0);
  not not_13 (not_13_out, A2);
  not not_14 (not_14_out, A4);
  not not_15 (not_15_out, A5);
  not not_16 (not_16_out, A0);
  not not_17 (not_17_out, A2);
  not not_18 (not_18_out, A5);
  not not_19 (not_19_out, A1);
  not not_20 (not_20_out, A5);
  not not_21 (not_21_out, A0);
  not not_22 (not_22_out, A1);
  not not_23 (not_23_out, A2);
  not not_24 (not_24_out, A4);
  not not_25 (not_25_out, A0);
  not not_26 (not_26_out, A1);
  not not_27 (not_27_out, A2);
  not not_28 (not_28_out, A5);
  and and_1 (and_1_out, not_1_out, not_2_out, A2, not_3_out, A4, A5);
  and and_2 (and_2_out, not_4_out, A1, not_5_out, not_6_out, A4, A5);
  and and_3 (and_3_out, A0, A1, not_7_out, A3, not_8_out, not_9_out);
  and and_4 (and_4_out, A0, A1, not_10_out, A3, not_11_out, A5);
  and and_5 (and_5_out, not_12_out, A1, not_13_out, A3, not_14_out, not_15_out);
  and and_6 (and_6_out, not_16_out, A1, not_17_out, A3, A4, not_18_out);
  and and_7 (and_7_out, not_19_out, A3, A4, not_20_out);
  and and_8 (and_8_out, not_21_out, not_22_out, not_23_out, A3, not_24_out, A5);
  and and_9 (and_9_out, not_25_out, not_26_out, not_27_out, A3, A4, not_28_out);
  or or_1 (x, and_1_out, and_2_out, and_3_out, and_4_out, and_5_out, and_6_out, and_7_out, and_8_out, and_9_out);
endmodule

module T (
  input  A0,
  input  A1,
  input  A2,
  input  A3,
  input  A4,
  input  A5,
  output x
);

  or or_1 (x, A0, A1, A2, A3, A4, A5, 1'b1);
endmodule
